// Logisim project leg_main.circ as structural Verilog: 5 circuits, main circuit main
module main (
  input  [7:0] Input,
  input  in_2,
  output [7:0] Output
);

  wire button_1_out, CLK, ENTER_out, equality_1_equal, equality_2_equal, equality_3_equal, equality_4_equal,
       equality_5_equal, equality_6_equal, equality_7_equal, equality_8_equal, equality_9_equal,
       equality_11_equal, equality_12_equal, equality_13_equal, equality_14_equal, equality_15_equal,
       equality_16_equal, equality_17_equal, equality_18_equal, equality_19_equal, equality_20_equal,
       equality_21_equal, equality_22_equal, equality_23_equal, equality_24_equal, not_1_out, not_2_out,
       not_3_out, O, or_1_out, or_2_out, pull_resistor_1_node, small_or_1_out_3;
  wire [7:0] alu_1_r, controlled_buffer_1_out, controlled_buffer_3_out, controlled_buffer_5_out,
       controlled_buffer_6_out, controlled_buffer_7_out, controlled_buffer_8_out, controlled_buffer_9_out,
       controlled_buffer_10_out, controlled_buffer_12_out, controlled_buffer_13_out,
       controlled_buffer_14_out, controlled_buffer_21_out, INP, memory_8_bit_1_stored_data,
       memory_8_bit_3_stored_data, memory_8_bit_4_stored_data, memory_8_bit_5_stored_data,
       memory_8_bit_6_stored_data, memory_8_bit_7_stored_data, memory_8_bit_8_stored_data, multiplexer_1_out,
       multiplexer_2_out, PROGRAM_p2, PROGRAM_p4, PROGRAM_p5, PROGRAM_p6, PROGRAM_p7, ram_1_dout,
       slider_1_out;
  wire [9:0] PROGRAM_p3;
  wire [15:0] mult_by_4_1_product_16_bit, multiplier_8_bit_1_product_16_bit;
  wire [63:0] TK_CNT;

  // Probe on TK_CNT
  // Probe on PROGRAM_p3
  Button button_1 (.out(button_1_out));
  Multiplexer #(.width(8)) multiplexer_1 (
    .in0(controlled_buffer_1_out), .in1({8{1'b0}}), .out(multiplexer_1_out), .sel(button_1_out));
  // ROM #(.addrWidth(10), .line("quad")) PROGRAM: pin names not known; wires that end beside it: 8'h4, PROGRAM_p2, PROGRAM_p3, PROGRAM_p4, PROGRAM_p5, PROGRAM_p6, PROGRAM_p7
  bit_crusher bit_crusher_1 (.in_1(multiplier_8_bit_1_product_16_bit), .out_2(PROGRAM_p3));
  multiplier_8_bit multiplier_8_bit_1 (
    .ARGUMENT_1(8'h4), .ARGUMENT_2(PROGRAM_p2), .PRODUCT_16_BIT(multiplier_8_bit_1_product_16_bit));  // open: LOWER_BYTE, UPPER_BYTE
  // Probe on PROGRAM_p2
  Counter counter_1 (
    .load(small_or_1_out_3), .clk(CLK), .D(multiplexer_1_out), .Q(PROGRAM_p2));  // open: clr, up, count, carry
  small_or small_or_1 (.in_1(button_1_out), .in_2(or_1_out), .out_3(small_or_1_out_3));
  RAM #(.asyncread("true")) ram_1 (
    .addr(memory_8_bit_3_stored_data), .we(equality_2_equal), .oe(equality_1_equal), .clk(CLK),
    .din(controlled_buffer_13_out), .dout(ram_1_dout));
  _7_Segment_Display u_7_segment_display_1 ();  // open: g, f, a, b, e, d, c, dp
  // BCD_to_7_Segment_decoder bcd_to_7_segment_decoder_1: pin names not known
  memory_8_bit memory_8_bit_1 (
    .DATA_IN(Output), .CLOCK(CLK), .SAVE(O), .STORED_DATA(memory_8_bit_1_stored_data));  // open: LOAD, DATA_OUT
  // Probe on memory_8_bit_1_stored_data
  // Binary_to_BCD_converter #(.binvalue(8)) binary_to_bcd_converter_1: pin names not known; wires that end beside it: memory_8_bit_1_stored_data
  Clock clock_1 (.out(CLK));
  _7_Segment_Display u_7_segment_display_2 ();  // open: g, f, a, b, e, d, c, dp
  // BCD_to_7_Segment_decoder bcd_to_7_segment_decoder_2: pin names not known
  Slider slider_1 (.out(slider_1_out));
  _7_Segment_Display u_7_segment_display_3 ();  // open: g, f, a, b, e, d, c, dp
  // BCD_to_7_Segment_decoder bcd_to_7_segment_decoder_3: pin names not known
  assign controlled_buffer_1_out = equality_3_equal ? controlled_buffer_3_out : 8'bz;  // Controlled_Buffer controlled_buffer_1
  or or_1 (or_1_out, pull_resistor_1_node, equality_3_equal);
  // Probe on mult_by_4_1_product_16_bit
  mult_by_4 mult_by_4_1 (.ARGUMENT_1(controlled_buffer_1_out), .PRODUCT_16_BIT(mult_by_4_1_product_16_bit));
  // Probe on ram_1_dout
  equality equality_1 (.ARG_2(8'h3f), .ARG_1(PROGRAM_p5), .EQUAL(equality_1_equal));
  equality equality_2 (.ARG_2(8'h3e), .ARG_1(PROGRAM_p7), .EQUAL(equality_2_equal));
  memory_8_bit memory_8_bit_2 (
    .DATA_IN(slider_1_out), .CLOCK(CLK), .SAVE(ENTER_out), .STORED_DATA(INP));  // open: LOAD, DATA_OUT
  // Probe on INP
  // Probe on INP
  Button ENTER (.out(ENTER_out));
  not not_1 (not_1_out, or_2_out);
  or or_2 (or_2_out, equality_1_equal, equality_2_equal);
  equality equality_3 (.ARG_2(PROGRAM_p7), .ARG_1(8'h6), .EQUAL(equality_3_equal));
  assign controlled_buffer_1_out = pull_resistor_1_node ? PROGRAM_p7 : 8'bz;  // Controlled_Buffer controlled_buffer_2
  Pull_Resistor pull_resistor_1 (.node(pull_resistor_1_node));
  assign controlled_buffer_3_out = or_2_out ? ram_1_dout : 8'bz;  // Controlled_Buffer controlled_buffer_3
  // Probe on PROGRAM_p4
  // Probe on PROGRAM_p5
  // Probe on PROGRAM_p6
  // Probe on PROGRAM_p7
  assign controlled_buffer_3_out = not_1_out ? alu_1_r : 8'bz;  // Controlled_Buffer controlled_buffer_4
  ALU alu_1 (
    .Clock(CLK), .OPCODE(PROGRAM_p4), .ARG_1(controlled_buffer_13_out), .ARG_2(controlled_buffer_12_out),
    .R(alu_1_r));
  COND cond_1 (
    .OPCODE(PROGRAM_p4), .ARG_1(controlled_buffer_13_out), .ARG_2(controlled_buffer_12_out),
    .RESULT(pull_resistor_1_node));
  equality equality_4 (.ARG_2({8{1'b0}}), .ARG_1(PROGRAM_p7), .EQUAL(equality_4_equal));
  equality equality_5 (.ARG_2(8'h1), .ARG_1(PROGRAM_p7), .EQUAL(equality_5_equal));
  equality equality_6 (.ARG_2(8'h2), .ARG_1(PROGRAM_p7), .EQUAL(equality_6_equal));
  equality equality_7 (.ARG_2(8'h3), .ARG_1(PROGRAM_p7), .EQUAL(equality_7_equal));
  equality equality_8 (.ARG_2(8'h4), .ARG_1(PROGRAM_p7), .EQUAL(equality_8_equal));
  equality equality_9 (.ARG_2(8'h5), .ARG_1(PROGRAM_p7), .EQUAL(equality_9_equal));
  equality equality_10 (.ARG_2(8'h7), .ARG_1(PROGRAM_p7), .EQUAL(O));
  assign controlled_buffer_5_out = equality_4_equal ? controlled_buffer_3_out : 8'bz;  // Controlled_Buffer controlled_buffer_5
  assign controlled_buffer_6_out = equality_5_equal ? controlled_buffer_3_out : 8'bz;  // Controlled_Buffer controlled_buffer_6
  assign controlled_buffer_7_out = equality_6_equal ? controlled_buffer_3_out : 8'bz;  // Controlled_Buffer controlled_buffer_7
  assign controlled_buffer_8_out = equality_7_equal ? controlled_buffer_3_out : 8'bz;  // Controlled_Buffer controlled_buffer_8
  assign controlled_buffer_9_out = equality_8_equal ? controlled_buffer_3_out : 8'bz;  // Controlled_Buffer controlled_buffer_9
  assign controlled_buffer_10_out = equality_9_equal ? controlled_buffer_3_out : 8'bz;  // Controlled_Buffer controlled_buffer_10
  assign Output = O ? controlled_buffer_3_out : 8'bz;  // Controlled_Buffer controlled_buffer_11
  assign controlled_buffer_12_out = PROGRAM_p4[6] ? PROGRAM_p6 : 8'bz;  // Controlled_Buffer controlled_buffer_12
  // Probe on memory_8_bit_3_stored_data
  memory_8_bit memory_8_bit_3 (
    .DATA_IN(controlled_buffer_5_out), .CLOCK(CLK), .SAVE(equality_4_equal),
    .STORED_DATA(memory_8_bit_3_stored_data));  // open: LOAD, DATA_OUT
  // Probe on memory_8_bit_4_stored_data
  memory_8_bit memory_8_bit_4 (
    .DATA_IN(controlled_buffer_6_out), .CLOCK(CLK), .SAVE(equality_5_equal),
    .STORED_DATA(memory_8_bit_4_stored_data));  // open: LOAD, DATA_OUT
  // Probe on memory_8_bit_5_stored_data
  memory_8_bit memory_8_bit_5 (
    .DATA_IN(controlled_buffer_7_out), .CLOCK(CLK), .SAVE(equality_6_equal),
    .STORED_DATA(memory_8_bit_5_stored_data));  // open: LOAD, DATA_OUT
  // Probe on memory_8_bit_6_stored_data
  memory_8_bit memory_8_bit_6 (
    .DATA_IN(controlled_buffer_8_out), .CLOCK(CLK), .SAVE(equality_7_equal),
    .STORED_DATA(memory_8_bit_6_stored_data));  // open: LOAD, DATA_OUT
  // Probe on memory_8_bit_7_stored_data
  memory_8_bit memory_8_bit_7 (
    .DATA_IN(controlled_buffer_9_out), .CLOCK(CLK), .SAVE(equality_8_equal),
    .STORED_DATA(memory_8_bit_7_stored_data));  // open: LOAD, DATA_OUT
  // Probe on memory_8_bit_8_stored_data
  memory_8_bit memory_8_bit_8 (
    .DATA_IN(controlled_buffer_10_out), .CLOCK(CLK), .SAVE(equality_9_equal),
    .STORED_DATA(memory_8_bit_8_stored_data));  // open: LOAD, DATA_OUT
  Multiplexer #(.width(8)) multiplexer_2 (.in0(INP), .in1(Input), .out(multiplexer_2_out), .sel(in_2));
  equality equality_11 (.ARG_2({8{1'b0}}), .ARG_1(PROGRAM_p6), .EQUAL(equality_11_equal));
  equality equality_12 (.ARG_2(8'h1), .ARG_1(PROGRAM_p6), .EQUAL(equality_12_equal));
  equality equality_13 (.ARG_2(8'h2), .ARG_1(PROGRAM_p6), .EQUAL(equality_13_equal));
  equality equality_14 (.ARG_2(8'h3), .ARG_1(PROGRAM_p6), .EQUAL(equality_14_equal));
  equality equality_15 (.ARG_2(8'h4), .ARG_1(PROGRAM_p6), .EQUAL(equality_15_equal));
  equality equality_16 (.ARG_2(8'h5), .ARG_1(PROGRAM_p6), .EQUAL(equality_16_equal));
  equality equality_17 (.ARG_2(8'h7), .ARG_1(PROGRAM_p6), .EQUAL(equality_17_equal));
  assign controlled_buffer_13_out = PROGRAM_p4[7] ? PROGRAM_p5 : 8'bz;  // Controlled_Buffer controlled_buffer_13
  assign controlled_buffer_14_out = equality_11_equal ? memory_8_bit_3_stored_data : 8'bz;  // Controlled_Buffer controlled_buffer_14
  assign controlled_buffer_14_out = equality_12_equal ? memory_8_bit_4_stored_data : 8'bz;  // Controlled_Buffer controlled_buffer_15
  assign controlled_buffer_14_out = equality_13_equal ? memory_8_bit_5_stored_data : 8'bz;  // Controlled_Buffer controlled_buffer_16
  assign controlled_buffer_14_out = equality_14_equal ? memory_8_bit_6_stored_data : 8'bz;  // Controlled_Buffer controlled_buffer_17
  assign controlled_buffer_14_out = equality_15_equal ? memory_8_bit_7_stored_data : 8'bz;  // Controlled_Buffer controlled_buffer_18
  assign controlled_buffer_14_out = equality_16_equal ? memory_8_bit_8_stored_data : 8'bz;  // Controlled_Buffer controlled_buffer_19
  assign controlled_buffer_14_out = equality_17_equal ? multiplexer_2_out : 8'bz;  // Controlled_Buffer controlled_buffer_20
  not not_2 (not_2_out, PROGRAM_p4[7]);
  equality equality_18 (.ARG_2({8{1'b0}}), .ARG_1(PROGRAM_p5), .EQUAL(equality_18_equal));
  assign controlled_buffer_21_out = equality_18_equal ? memory_8_bit_3_stored_data : 8'bz;  // Controlled_Buffer controlled_buffer_21
  equality equality_19 (.ARG_2(8'h1), .ARG_1(PROGRAM_p5), .EQUAL(equality_19_equal));
  assign controlled_buffer_21_out = equality_19_equal ? memory_8_bit_4_stored_data : 8'bz;  // Controlled_Buffer controlled_buffer_22
  equality equality_20 (.ARG_2(8'h2), .ARG_1(PROGRAM_p5), .EQUAL(equality_20_equal));
  assign controlled_buffer_21_out = equality_20_equal ? memory_8_bit_5_stored_data : 8'bz;  // Controlled_Buffer controlled_buffer_23
  equality equality_21 (.ARG_2(8'h3), .ARG_1(PROGRAM_p5), .EQUAL(equality_21_equal));
  assign controlled_buffer_21_out = equality_21_equal ? memory_8_bit_6_stored_data : 8'bz;  // Controlled_Buffer controlled_buffer_24
  equality equality_22 (.ARG_2(8'h4), .ARG_1(PROGRAM_p5), .EQUAL(equality_22_equal));
  assign controlled_buffer_21_out = equality_22_equal ? memory_8_bit_7_stored_data : 8'bz;  // Controlled_Buffer controlled_buffer_25
  equality equality_23 (.ARG_2(8'h5), .ARG_1(PROGRAM_p5), .EQUAL(equality_23_equal));
  assign controlled_buffer_21_out = equality_23_equal ? memory_8_bit_8_stored_data : 8'bz;  // Controlled_Buffer controlled_buffer_26
  equality equality_24 (.ARG_2(8'h7), .ARG_1(PROGRAM_p5), .EQUAL(equality_24_equal));
  assign controlled_buffer_21_out = equality_24_equal ? multiplexer_2_out : 8'bz;  // Controlled_Buffer controlled_buffer_27
  not not_3 (not_3_out, PROGRAM_p4[6]);
  assign controlled_buffer_13_out = not_2_out ? controlled_buffer_21_out : 8'bz;  // Controlled_Buffer controlled_buffer_28
  assign controlled_buffer_12_out = not_3_out ? controlled_buffer_14_out : 8'bz;  // Controlled_Buffer controlled_buffer_29
  Counter #(.max('hffffffffffffffff), .width(64)) counter_2 (
    .clk(CLK), .Q(TK_CNT));  // open: clr, load, up, count, D, carry
  // Probe on TK_CNT

  // Other names for the same wires on the sheet: OUTP[7:0] = Output

  // Notes on the sheet:
  //   Tick Count
  //   Reset
  //   contents of PROGRAM (hex, n*v repeats v):
  //   e0 0 0 8 28*0 e0 0 0 22 c0 0 0 0 c0 0 0 1 60 1 f 21 40 1 0 5 40 1 1 2 60 2 f 17 40 5 0 0 40 3f 0 3
  //   40 2 0 0 40 3f 0 4 25 4 3 15 40 2 0 5 40 2 1 2 e0 0 0 e 40 1 0 0 40 3f 0 3 40 5 0 0 40 3f 0 4 40 5 0
  //   0 40 3 0 3e 40 1 0 0 40 4 0 3e 40 1 1 1 e0 0 0 b e0 0 0 21 c0 0 0 0 c0 f 0 3e 40 0 1 0 c0 e 0 3e 40
  //   0 1 0 c0 d 0 3e 40 0 1 0 c0 c 0 3e 40 0 1 0 c0 b 0 3e 40 0 1 0 c0 a 0 3e 40 0 1 0 c0 9 0 3e 40 0 1 0
  //   c0 8 0 3e 40 0 1 0 c0 7 0 3e 40 0 1 0 c0 6 0 3e 40 0 1 0 c0 5 0 3e 40 0 1 0 c0 4 0 3e 40 0 1 0 c0 3
  //   0 3e 40 0 1 0 c0 2 0 3e 40 0 1 0 c0 1 0 3e e0 0 0 9
  //   Program Memory
  //   Counter
  //   RAM Load
  //   RAM Save
  //   Output
  //   Enter Input Value
  //   RAM Address
  //   RAM Save Value
  //   RAM Value
  //   S
  //   Send
  //   Opcode
  //   Argument 1
  //   Argument 2
  //   Result / Jump Address
  //   L
  //   Result
  //   Result
  //   Result
  //   Result
  //   Result
  //   Result
  //   Result
  //   8-Bit ALU
  //   Condition
  //   RAM Address
  //   Register 1
  //   Register 2
  //   Register 3
  //   Register 4
  //   Register 5
  //   ARG 2
  //   ARG 2
  //   ARG 2
  //   ARG 2
  //   ARG 2
  //   ARG 2
  //   ARG 2
  //   Immediate Mode Switch
  //   Opcode
  //   ARG 2
  //   ARG 1
  //   ARG 1
  //   ARG 1
  //   ARG 1
  //   ARG 1
  //   ARG 1
  //   ARG 1
  //   ARG 1
endmodule

module ALU (
  input  [7:0] OPCODE,
  input  [7:0] ARG_1,
  input  [7:0] ARG_2,
  input  Clock,
  output [7:0] R
);

  wire equality_1_equal, equality_2_equal, equality_3_equal, equality_4_equal, equality_5_equal,
       equality_6_equal, equality_7_equal, equality_8_equal, equality_9_equal, equality_10_equal;
  wire [7:0] adder_8_bit_1_result, adder_8_bit_2_result, and_8_bit_1_result, and_8_bit_2_result,
       divider_8_bit_1_quotient, divider_8_bit_1_remainder, memory_8_bit_1_stored_data,
       multiplier_8_bit_1_lower_byte, multiplier_8_bit_1_upper_byte, negator_8_bit_1_neg_arg,
       not_8_bit_1_out_2, or_8_bit_1_result, xor_8_bit_1_result;
  wire [15:0] multiplier_8_bit_1_product_16_bit;

  // Probe on OPCODE
  // Probe on ARG_1
  // Probe on ARG_2
  and_8_bit and_8_bit_1 (.ARG_2(8'h1f), .ARG_1(OPCODE), .RESULT(and_8_bit_1_result));
  adder_8_bit adder_8_bit_1 (.ARG_2(ARG_2), .ARG_1(ARG_1), .RESULT(adder_8_bit_1_result));  // open: CARRY_IN, CARRY_OUT
  negator_8_bit negator_8_bit_1 (.ARG_IN(ARG_2), .NEG_ARG(negator_8_bit_1_neg_arg));
  and_8_bit and_8_bit_2 (.ARG_2(ARG_2), .ARG_1(ARG_1), .RESULT(and_8_bit_2_result));
  or_8_bit or_8_bit_1 (.ARG_2(ARG_2), .ARG_1(ARG_1), .RESULT(or_8_bit_1_result));
  not_8_bit not_8_bit_1 (.in_1(ARG_1), .out_2(not_8_bit_1_out_2));
  xor_8_bit xor_8_bit_1 (.ARG_2(ARG_2), .ARG_1(ARG_1), .RESULT(xor_8_bit_1_result));
  assign R = equality_1_equal ? adder_8_bit_1_result : 8'bz;  // Controlled_Buffer controlled_buffer_1
  equality equality_1 (.ARG_2({8{1'b0}}), .ARG_1(and_8_bit_1_result), .EQUAL(equality_1_equal));
  assign R = equality_2_equal ? adder_8_bit_2_result : 8'bz;  // Controlled_Buffer controlled_buffer_2
  adder_8_bit adder_8_bit_2 (
    .ARG_2(negator_8_bit_1_neg_arg), .ARG_1(ARG_1), .RESULT(adder_8_bit_2_result));  // open: CARRY_IN, CARRY_OUT
  equality equality_2 (.ARG_2(8'h1), .ARG_1(and_8_bit_1_result), .EQUAL(equality_2_equal));
  assign R = equality_3_equal ? and_8_bit_2_result : 8'bz;  // Controlled_Buffer controlled_buffer_3
  equality equality_3 (.ARG_2(8'h2), .ARG_1(and_8_bit_1_result), .EQUAL(equality_3_equal));
  assign R = equality_4_equal ? or_8_bit_1_result : 8'bz;  // Controlled_Buffer controlled_buffer_4
  equality equality_4 (.ARG_2(8'h3), .ARG_1(and_8_bit_1_result), .EQUAL(equality_4_equal));
  assign R = equality_5_equal ? not_8_bit_1_out_2 : 8'bz;  // Controlled_Buffer controlled_buffer_5
  equality equality_5 (.ARG_2(8'h4), .ARG_1(and_8_bit_1_result), .EQUAL(equality_5_equal));
  assign R = equality_6_equal ? xor_8_bit_1_result : 8'bz;  // Controlled_Buffer controlled_buffer_6
  equality equality_6 (.ARG_2(8'h5), .ARG_1(and_8_bit_1_result), .EQUAL(equality_6_equal));
  // Probe on multiplier_8_bit_1_product_16_bit
  multiplier_8_bit multiplier_8_bit_1 (
    .ARGUMENT_1(ARG_1), .ARGUMENT_2(ARG_2), .LOWER_BYTE(multiplier_8_bit_1_lower_byte),
    .UPPER_BYTE(multiplier_8_bit_1_upper_byte), .PRODUCT_16_BIT(multiplier_8_bit_1_product_16_bit));
  memory_8_bit memory_8_bit_1 (
    .DATA_IN(multiplier_8_bit_1_upper_byte), .CLOCK(Clock), .SAVE(equality_7_equal),
    .STORED_DATA(memory_8_bit_1_stored_data));  // open: LOAD, DATA_OUT
  divider_8_bit divider_8_bit_1 (
    .ARGUMENT_1(ARG_1), .ARGUMENT_2(ARG_2), .QUOTIENT(divider_8_bit_1_quotient),
    .REMAINDER(divider_8_bit_1_remainder));
  // Probe on R
  assign R = equality_7_equal ? multiplier_8_bit_1_lower_byte : 8'bz;  // Controlled_Buffer controlled_buffer_7
  equality equality_7 (.ARG_2(8'he), .ARG_1(and_8_bit_1_result), .EQUAL(equality_7_equal));
  assign R = equality_8_equal ? memory_8_bit_1_stored_data : 8'bz;  // Controlled_Buffer controlled_buffer_8
  equality equality_8 (.ARG_2(8'hf), .ARG_1(and_8_bit_1_result), .EQUAL(equality_8_equal));
  assign R = equality_9_equal ? divider_8_bit_1_quotient : 8'bz;  // Controlled_Buffer controlled_buffer_9
  equality equality_9 (.ARG_2(8'h10), .ARG_1(and_8_bit_1_result), .EQUAL(equality_9_equal));
  assign R = equality_10_equal ? divider_8_bit_1_remainder : 8'bz;  // Controlled_Buffer controlled_buffer_10
  equality equality_10 (.ARG_2(8'h11), .ARG_1(and_8_bit_1_result), .EQUAL(equality_10_equal));

  // Other names for the same wires on the sheet: CLK = Clock

  // Notes on the sheet:
  //   Opcode
  //   Argument 1
  //   Argument 2
  //   Addition
  //   Subtraction
  //   Logic AND
  //   Logic OR
  //   Logic NOT
  //   Logic XOR
  //   Multiplication
  //   Lower Byte
  //   Upper Byte
  //   Division
  //   Modulus
  //   Result
endmodule

module COND (
  input  [7:0] OPCODE,
  input  [7:0] ARG_1,
  input  [7:0] ARG_2,
  output RESULT
);

  wire equality_1_equal, equality_2_equal, equality_3_equal, equality_4_equal, equality_5_equal,
       equality_6_equal, equality_7_equal, equality_8_equal, equality_9_equal, equality_10_equal,
       equality_11_equal, equality_12_equal, equality_13_equal, equality_14_equal, equality_15_equal,
       equality_16_equal, less_signed_1_less, less_signed_2_less, less_unsigned_1_less, not_1_out, not_2_out,
       not_3_out, not_4_out, not_5_out, or_1_out, or_2_out, or_3_out;
  wire [7:0] and_8_bit_1_result;

  // Probe on OPCODE
  // Probe on ARG_1
  // Probe on ARG_2
  and_8_bit and_8_bit_1 (.ARG_2(8'h3f), .ARG_1(OPCODE), .RESULT(and_8_bit_1_result));
  equality equality_1 (.ARG_2(ARG_2), .ARG_1(ARG_1), .EQUAL(equality_1_equal));
  equality equality_2 (.ARG_2(ARG_2), .ARG_1(ARG_1), .EQUAL(equality_2_equal));
  less_unsigned less_unsigned_1 (.ARG_1(ARG_1), .ARG_2(ARG_2), .LESS(less_unsigned_1_less));
  equality equality_3 (.ARG_2(ARG_2), .ARG_1(ARG_1), .EQUAL(equality_3_equal));
  assign RESULT = equality_4_equal ? equality_1_equal : 1'bz;  // Controlled_Buffer controlled_buffer_1
  equality equality_4 (.ARG_2(8'h20), .ARG_1(and_8_bit_1_result), .EQUAL(equality_4_equal));
  assign RESULT = equality_5_equal ? not_1_out : 1'bz;  // Controlled_Buffer controlled_buffer_2
  not not_1 (not_1_out, equality_2_equal);
  equality equality_5 (.ARG_2(8'h21), .ARG_1(and_8_bit_1_result), .EQUAL(equality_5_equal));
  assign RESULT = equality_6_equal ? less_unsigned_1_less : 1'bz;  // Controlled_Buffer controlled_buffer_3
  equality equality_6 (.ARG_2(8'h22), .ARG_1(and_8_bit_1_result), .EQUAL(equality_6_equal));
  or or_1 (or_1_out, less_unsigned_1_less, equality_3_equal);
  assign RESULT = equality_7_equal ? or_1_out : 1'bz;  // Controlled_Buffer controlled_buffer_4
  equality equality_7 (.ARG_2(8'h23), .ARG_1(and_8_bit_1_result), .EQUAL(equality_7_equal));
  not not_2 (not_2_out, or_1_out);
  assign RESULT = equality_8_equal ? not_2_out : 1'bz;  // Controlled_Buffer controlled_buffer_5
  equality equality_8 (.ARG_2(8'h24), .ARG_1(and_8_bit_1_result), .EQUAL(equality_8_equal));
  not not_3 (not_3_out, less_unsigned_1_less);
  assign RESULT = equality_9_equal ? not_3_out : 1'bz;  // Controlled_Buffer controlled_buffer_6
  equality equality_9 (.ARG_2(8'h25), .ARG_1(and_8_bit_1_result), .EQUAL(equality_9_equal));
  less_signed less_signed_1 (.ARG_1(ARG_1), .ARG_2(ARG_2), .LESS(less_signed_1_less));
  or or_2 (or_2_out, less_signed_1_less, less_signed_2_less);
  less_signed less_signed_2 (.ARG_1(ARG_1), .ARG_2(ARG_2), .LESS(less_signed_2_less));
  not not_4 (not_4_out, or_2_out);
  not not_5 (not_5_out, less_signed_1_less);
  or or_3 (or_3_out, equality_16_equal, equality_15_equal, equality_14_equal);
  // Probe on RESULT
  assign RESULT = equality_10_equal ? less_signed_1_less : 1'bz;  // Controlled_Buffer controlled_buffer_7
  equality equality_10 (.ARG_2(8'h26), .ARG_1(and_8_bit_1_result), .EQUAL(equality_10_equal));
  assign RESULT = equality_11_equal ? or_2_out : 1'bz;  // Controlled_Buffer controlled_buffer_8
  equality equality_11 (.ARG_2(8'h27), .ARG_1(and_8_bit_1_result), .EQUAL(equality_11_equal));
  assign RESULT = equality_12_equal ? not_4_out : 1'bz;  // Controlled_Buffer controlled_buffer_9
  equality equality_12 (.ARG_2(8'h28), .ARG_1(and_8_bit_1_result), .EQUAL(equality_12_equal));
  assign RESULT = equality_13_equal ? not_5_out : 1'bz;  // Controlled_Buffer controlled_buffer_10
  equality equality_13 (.ARG_2(8'h29), .ARG_1(and_8_bit_1_result), .EQUAL(equality_13_equal));
  assign RESULT = or_3_out ? 1'b1 : 1'bz;  // Controlled_Buffer controlled_buffer_11
  equality equality_14 (.ARG_2(8'h38), .ARG_1(and_8_bit_1_result), .EQUAL(equality_14_equal));
  equality equality_15 (.ARG_2(8'h39), .ARG_1(and_8_bit_1_result), .EQUAL(equality_15_equal));
  equality equality_16 (.ARG_2(8'h3a), .ARG_1(and_8_bit_1_result), .EQUAL(equality_16_equal));

  // Notes on the sheet:
  //   Opcode
  //   Argument 1
  //   Argument 2
  //   =
  //   !=
  //   (US) <
  //   (US) <=
  //   (US) >
  //   (US) >=
  //   (S) <
  //   (S) <=
  //   (S) >
  //   (S) >=
  //   Call, Return, End
  //   Result
endmodule

module small_or (
  input  in_1,
  input  in_2,
  output out_3
);

  or or_1 (out_3, in_1, in_2);
endmodule

module bit_crusher (
  input  [15:0] in_1,
  output [9:0] out_2
);


  assign out_2 = in_1[9:0];
endmodule
