// Logisim project leg_main.circ as structural Verilog: 2 circuits, main circuit main
module main (
  input  [7:0] in_1,
  output [7:0] Output
);

  wire button_1_out, CLK, equality_1_equal, equality_2_equal, equality_3_equal, equality_4_equal,
       equality_5_equal, equality_6_equal, equality_7_equal, equality_8_equal, equality_9_equal,
       equality_10_equal, equality_11_equal, equality_12_equal, equality_13_equal, equality_14_equal,
       equality_15_equal, equality_16_equal, equality_17_equal, equality_18_equal, equality_19_equal,
       equality_20_equal, equality_21_equal, not_1_out, not_2_out;
  wire [7:0] alu_1_result, controlled_buffer_1_out, controlled_buffer_2_out, controlled_buffer_3_out,
       controlled_buffer_4_out, controlled_buffer_5_out, controlled_buffer_6_out, controlled_buffer_8_out,
       controlled_buffer_9_out, controlled_buffer_10_out, controlled_buffer_17_out, counter_1_q,
       memory_8_bit_1_stored_data, memory_8_bit_2_stored_data, memory_8_bit_3_stored_data,
       memory_8_bit_4_stored_data, memory_8_bit_5_stored_data, memory_8_bit_6_stored_data, multiplier_1_out,
       PROGRAM_p2, PROGRAM_p3, PROGRAM_p4, PROGRAM_p5;

  // Probe on multiplier_1_out
  Multiplier multiplier_1 (.a(8'h4), .b(counter_1_q), .out(multiplier_1_out));  // open: cin, cout
  Button button_1 (.out(button_1_out));
  // ROM #(.line("quad")) PROGRAM: pin names not known; wires that end beside it: multiplier_1_out, PROGRAM_p2, PROGRAM_p3, PROGRAM_p4, PROGRAM_p5
  // Probe on counter_1_q
  Counter #(.max('h3f)) counter_1 (
    .load(button_1_out), .clk(CLK), .D({8{1'b0}}), .Q(counter_1_q));  // open: clr, up, count, carry
  Clock clock_1 (.out(CLK));
  // Probe on PROGRAM_p2
  // Probe on PROGRAM_p3
  // Probe on PROGRAM_p4
  // Probe on PROGRAM_p5
  ALU alu_1 (
    .Clock(CLK), .in_1(PROGRAM_p2), .in_2(controlled_buffer_9_out), .in_3(controlled_buffer_8_out),
    .Result(alu_1_result));
  equality equality_1 (.ARG_2({8{1'b0}}), .ARG_1(PROGRAM_p5), .EQUAL(equality_1_equal));
  equality equality_2 (.ARG_2(8'h1), .ARG_1(PROGRAM_p5), .EQUAL(equality_2_equal));
  equality equality_3 (.ARG_2(8'h2), .ARG_1(PROGRAM_p5), .EQUAL(equality_3_equal));
  equality equality_4 (.ARG_2(8'h3), .ARG_1(PROGRAM_p5), .EQUAL(equality_4_equal));
  equality equality_5 (.ARG_2(8'h4), .ARG_1(PROGRAM_p5), .EQUAL(equality_5_equal));
  equality equality_6 (.ARG_2(8'h5), .ARG_1(PROGRAM_p5), .EQUAL(equality_6_equal));
  equality equality_7 (.ARG_2(8'h7), .ARG_1(PROGRAM_p5), .EQUAL(equality_7_equal));
  assign controlled_buffer_1_out = equality_1_equal ? alu_1_result : 8'bz;  // Controlled_Buffer controlled_buffer_1
  assign controlled_buffer_2_out = equality_2_equal ? alu_1_result : 8'bz;  // Controlled_Buffer controlled_buffer_2
  assign controlled_buffer_3_out = equality_3_equal ? alu_1_result : 8'bz;  // Controlled_Buffer controlled_buffer_3
  assign controlled_buffer_4_out = equality_4_equal ? alu_1_result : 8'bz;  // Controlled_Buffer controlled_buffer_4
  assign controlled_buffer_5_out = equality_5_equal ? alu_1_result : 8'bz;  // Controlled_Buffer controlled_buffer_5
  assign controlled_buffer_6_out = equality_6_equal ? alu_1_result : 8'bz;  // Controlled_Buffer controlled_buffer_6
  assign Output = equality_7_equal ? alu_1_result : 8'bz;  // Controlled_Buffer controlled_buffer_7
  assign controlled_buffer_8_out = PROGRAM_p2[6] ? PROGRAM_p4 : 8'bz;  // Controlled_Buffer controlled_buffer_8
  // Probe on memory_8_bit_1_stored_data
  memory_8_bit memory_8_bit_1 (
    .DATA_IN(controlled_buffer_1_out), .CLOCK(CLK), .SAVE(equality_1_equal),
    .STORED_DATA(memory_8_bit_1_stored_data));  // open: LOAD, DATA_OUT
  // Probe on memory_8_bit_2_stored_data
  memory_8_bit memory_8_bit_2 (
    .DATA_IN(controlled_buffer_2_out), .CLOCK(CLK), .SAVE(equality_2_equal),
    .STORED_DATA(memory_8_bit_2_stored_data));  // open: LOAD, DATA_OUT
  // Probe on memory_8_bit_3_stored_data
  memory_8_bit memory_8_bit_3 (
    .DATA_IN(controlled_buffer_3_out), .CLOCK(CLK), .SAVE(equality_3_equal),
    .STORED_DATA(memory_8_bit_3_stored_data));  // open: LOAD, DATA_OUT
  // Probe on memory_8_bit_4_stored_data
  memory_8_bit memory_8_bit_4 (
    .DATA_IN(controlled_buffer_4_out), .CLOCK(CLK), .SAVE(equality_4_equal),
    .STORED_DATA(memory_8_bit_4_stored_data));  // open: LOAD, DATA_OUT
  // Probe on memory_8_bit_5_stored_data
  memory_8_bit memory_8_bit_5 (
    .DATA_IN(controlled_buffer_5_out), .CLOCK(CLK), .SAVE(equality_5_equal),
    .STORED_DATA(memory_8_bit_5_stored_data));  // open: LOAD, DATA_OUT
  // Probe on memory_8_bit_6_stored_data
  memory_8_bit memory_8_bit_6 (
    .DATA_IN(controlled_buffer_6_out), .CLOCK(CLK), .SAVE(equality_6_equal),
    .STORED_DATA(memory_8_bit_6_stored_data));  // open: LOAD, DATA_OUT
  equality equality_8 (.ARG_2({8{1'b0}}), .ARG_1(PROGRAM_p4), .EQUAL(equality_8_equal));
  equality equality_9 (.ARG_2(8'h1), .ARG_1(PROGRAM_p4), .EQUAL(equality_9_equal));
  equality equality_10 (.ARG_2(8'h2), .ARG_1(PROGRAM_p4), .EQUAL(equality_10_equal));
  equality equality_11 (.ARG_2(8'h3), .ARG_1(PROGRAM_p4), .EQUAL(equality_11_equal));
  equality equality_12 (.ARG_2(8'h4), .ARG_1(PROGRAM_p4), .EQUAL(equality_12_equal));
  equality equality_13 (.ARG_2(8'h5), .ARG_1(PROGRAM_p4), .EQUAL(equality_13_equal));
  equality equality_14 (.ARG_2(8'h7), .ARG_1(PROGRAM_p4), .EQUAL(equality_14_equal));
  assign controlled_buffer_9_out = PROGRAM_p2[7] ? PROGRAM_p3 : 8'bz;  // Controlled_Buffer controlled_buffer_9
  assign controlled_buffer_10_out = equality_8_equal ? memory_8_bit_1_stored_data : 8'bz;  // Controlled_Buffer controlled_buffer_10
  assign controlled_buffer_10_out = equality_9_equal ? memory_8_bit_2_stored_data : 8'bz;  // Controlled_Buffer controlled_buffer_11
  assign controlled_buffer_10_out = equality_10_equal ? memory_8_bit_3_stored_data : 8'bz;  // Controlled_Buffer controlled_buffer_12
  assign controlled_buffer_10_out = equality_11_equal ? memory_8_bit_4_stored_data : 8'bz;  // Controlled_Buffer controlled_buffer_13
  assign controlled_buffer_10_out = equality_12_equal ? memory_8_bit_5_stored_data : 8'bz;  // Controlled_Buffer controlled_buffer_14
  assign controlled_buffer_10_out = equality_13_equal ? memory_8_bit_6_stored_data : 8'bz;  // Controlled_Buffer controlled_buffer_15
  assign controlled_buffer_10_out = equality_14_equal ? in_1 : 8'bz;  // Controlled_Buffer controlled_buffer_16
  not not_1 (not_1_out, PROGRAM_p2[7]);
  equality equality_15 (.ARG_2({8{1'b0}}), .ARG_1(PROGRAM_p3), .EQUAL(equality_15_equal));
  assign controlled_buffer_17_out = equality_15_equal ? memory_8_bit_1_stored_data : 8'bz;  // Controlled_Buffer controlled_buffer_17
  equality equality_16 (.ARG_2(8'h1), .ARG_1(PROGRAM_p3), .EQUAL(equality_16_equal));
  assign controlled_buffer_17_out = equality_16_equal ? memory_8_bit_2_stored_data : 8'bz;  // Controlled_Buffer controlled_buffer_18
  equality equality_17 (.ARG_2(8'h2), .ARG_1(PROGRAM_p3), .EQUAL(equality_17_equal));
  assign controlled_buffer_17_out = equality_17_equal ? memory_8_bit_3_stored_data : 8'bz;  // Controlled_Buffer controlled_buffer_19
  equality equality_18 (.ARG_2(8'h3), .ARG_1(PROGRAM_p3), .EQUAL(equality_18_equal));
  assign controlled_buffer_17_out = equality_18_equal ? memory_8_bit_4_stored_data : 8'bz;  // Controlled_Buffer controlled_buffer_20
  equality equality_19 (.ARG_2(8'h4), .ARG_1(PROGRAM_p3), .EQUAL(equality_19_equal));
  assign controlled_buffer_17_out = equality_19_equal ? memory_8_bit_5_stored_data : 8'bz;  // Controlled_Buffer controlled_buffer_21
  equality equality_20 (.ARG_2(8'h5), .ARG_1(PROGRAM_p3), .EQUAL(equality_20_equal));
  assign controlled_buffer_17_out = equality_20_equal ? memory_8_bit_6_stored_data : 8'bz;  // Controlled_Buffer controlled_buffer_22
  equality equality_21 (.ARG_2(8'h7), .ARG_1(PROGRAM_p3), .EQUAL(equality_21_equal));
  assign controlled_buffer_17_out = equality_21_equal ? in_1 : 8'bz;  // Controlled_Buffer controlled_buffer_23
  not not_2 (not_2_out, PROGRAM_p2[6]);
  assign controlled_buffer_9_out = not_1_out ? controlled_buffer_17_out : 8'bz;  // Controlled_Buffer controlled_buffer_24
  assign controlled_buffer_8_out = not_2_out ? controlled_buffer_10_out : 8'bz;  // Controlled_Buffer controlled_buffer_25

  // Notes on the sheet:
  //   contents of PROGRAM (hex, n*v repeats v):
  //   c0 ff 0 1 c0 17 0 2 40 1 0 3 0 1 2 3 c0 92 17 4 41 1 16 3 c0 ff 0 1 c0 ff 0 2 e 1 2 5 f 40 0 4 d0 12
  //   2 4 d1 20 14 5 3a
  //   Program Memory
  //   Counter
  //   Opcode
  //   Argument 1
  //   Argument 2
  //   Result / Jump Address
  //   Result
  //   Result
  //   Result
  //   Result
  //   Result
  //   Result
  //   Result
  //   8-Bit ALU
  //   Register 0
  //   Register 1
  //   Register 2
  //   Register 3
  //   Register 4
  //   Register 5
  //   Input
  //   ARG 2
  //   ARG 2
  //   ARG 2
  //   ARG 2
  //   ARG 2
  //   ARG 2
  //   ARG 2
  //   Immediate Mode Switch
  //   Opcode
  //   ARG 2
  //   ARG 1
  //   ARG 1
  //   ARG 1
  //   ARG 1
  //   ARG 1
  //   ARG 1
  //   ARG 1
  //   ARG 1
endmodule

module ALU (
  input  [7:0] in_1,
  input  [7:0] in_2,
  input  [7:0] in_3,
  input  Clock,
  output [7:0] Result
);

  wire equality_1_equal, equality_2_equal, equality_3_equal, equality_4_equal, equality_5_equal,
       equality_6_equal, equality_7_equal, equality_8_equal, equality_9_equal, equality_10_equal;
  wire [7:0] adder_8_bit_1_result, adder_8_bit_2_result, and_8_bit_1_result, and_8_bit_2_result,
       divider_8_bit_1_quotient, divider_8_bit_1_remainder, memory_8_bit_1_stored_data,
       multiplier_8_bit_1_lower_byte, multiplier_8_bit_1_upper_byte, negator_8_bit_1_out_2,
       not_8_bit_1_out_2, or_8_bit_1_result, xor_8_bit_1_result;
  wire [15:0] multiplier_8_bit_1_product_16_bit;

  // Probe on in_1
  // Probe on in_2
  // Probe on in_3
  and_8_bit and_8_bit_1 (.ARG_2(8'h1f), .ARG_1(in_1), .RESULT(and_8_bit_1_result));
  adder_8_bit adder_8_bit_1 (.ARG_2(in_3), .ARG_1(in_2), .RESULT(adder_8_bit_1_result));  // open: CARRY_IN, CARRY_OUT
  negator_8_bit negator_8_bit_1 (.in_1(in_3), .out_2(negator_8_bit_1_out_2));
  and_8_bit and_8_bit_2 (.ARG_2(in_3), .ARG_1(in_2), .RESULT(and_8_bit_2_result));
  or_8_bit or_8_bit_1 (.ARG_2(in_3), .ARG_1(in_2), .RESULT(or_8_bit_1_result));
  not_8_bit not_8_bit_1 (.in_1(in_2), .out_2(not_8_bit_1_out_2));
  xor_8_bit xor_8_bit_1 (.ARG_2(in_3), .ARG_1(in_2), .RESULT(xor_8_bit_1_result));
  assign Result = equality_1_equal ? adder_8_bit_1_result : 8'bz;  // Controlled_Buffer controlled_buffer_1
  equality equality_1 (.ARG_2({8{1'b0}}), .ARG_1(and_8_bit_1_result), .EQUAL(equality_1_equal));
  assign Result = equality_2_equal ? adder_8_bit_2_result : 8'bz;  // Controlled_Buffer controlled_buffer_2
  adder_8_bit adder_8_bit_2 (
    .ARG_2(negator_8_bit_1_out_2), .ARG_1(in_2), .RESULT(adder_8_bit_2_result));  // open: CARRY_IN, CARRY_OUT
  equality equality_2 (.ARG_2(8'h1), .ARG_1(and_8_bit_1_result), .EQUAL(equality_2_equal));
  assign Result = equality_3_equal ? and_8_bit_2_result : 8'bz;  // Controlled_Buffer controlled_buffer_3
  equality equality_3 (.ARG_2(8'h2), .ARG_1(and_8_bit_1_result), .EQUAL(equality_3_equal));
  assign Result = equality_4_equal ? or_8_bit_1_result : 8'bz;  // Controlled_Buffer controlled_buffer_4
  equality equality_4 (.ARG_2(8'h3), .ARG_1(and_8_bit_1_result), .EQUAL(equality_4_equal));
  assign Result = equality_5_equal ? not_8_bit_1_out_2 : 8'bz;  // Controlled_Buffer controlled_buffer_5
  equality equality_5 (.ARG_2(8'h4), .ARG_1(and_8_bit_1_result), .EQUAL(equality_5_equal));
  assign Result = equality_6_equal ? xor_8_bit_1_result : 8'bz;  // Controlled_Buffer controlled_buffer_6
  equality equality_6 (.ARG_2(8'h5), .ARG_1(and_8_bit_1_result), .EQUAL(equality_6_equal));
  // Probe on multiplier_8_bit_1_product_16_bit
  multiplier_8_bit multiplier_8_bit_1 (
    .ARGUMENT_1(in_2), .ARGUMENT_2(in_3), .LOWER_BYTE(multiplier_8_bit_1_lower_byte),
    .UPPER_BYTE(multiplier_8_bit_1_upper_byte), .PRODUCT_16_BIT(multiplier_8_bit_1_product_16_bit));
  memory_8_bit memory_8_bit_1 (
    .DATA_IN(multiplier_8_bit_1_upper_byte), .CLOCK(Clock), .SAVE(equality_7_equal),
    .STORED_DATA(memory_8_bit_1_stored_data));  // open: LOAD, DATA_OUT
  divider_8_bit divider_8_bit_1 (
    .ARGUMENT_1(in_2), .ARGUMENT_2(in_3), .QUOTIENT(divider_8_bit_1_quotient),
    .REMAINDER(divider_8_bit_1_remainder));
  // Probe on Result
  assign Result = equality_7_equal ? multiplier_8_bit_1_lower_byte : 8'bz;  // Controlled_Buffer controlled_buffer_7
  equality equality_7 (.ARG_2(8'he), .ARG_1(and_8_bit_1_result), .EQUAL(equality_7_equal));
  assign Result = equality_8_equal ? memory_8_bit_1_stored_data : 8'bz;  // Controlled_Buffer controlled_buffer_8
  equality equality_8 (.ARG_2(8'hf), .ARG_1(and_8_bit_1_result), .EQUAL(equality_8_equal));
  assign Result = equality_9_equal ? divider_8_bit_1_quotient : 8'bz;  // Controlled_Buffer controlled_buffer_9
  equality equality_9 (.ARG_2(8'h10), .ARG_1(and_8_bit_1_result), .EQUAL(equality_9_equal));
  assign Result = equality_10_equal ? divider_8_bit_1_remainder : 8'bz;  // Controlled_Buffer controlled_buffer_10
  equality equality_10 (.ARG_2(8'h11), .ARG_1(and_8_bit_1_result), .EQUAL(equality_10_equal));

  // Other names for the same wires on the sheet: CLK = Clock

  // Notes on the sheet:
  //   Opcode
  //   Argument 1
  //   Argument 2
  //   Addition
  //   Subtraction
  //   Logic AND
  //   Logic OR
  //   Logic NOT
  //   Logic XOR
  //   Multiplication
  //   Lower Byte
  //   Upper Byte
  //   Division
  //   Modulus
endmodule
