// Logisim project Basic_8_Bit_Components.circ as structural Verilog: 10 circuits, main circuit switch_8_bit
module memory_8_bit (
  input  SAVE,
  input  LOAD,
  input  [7:0] DATA_IN,
  input  CLOCK,
  output [7:0] DATA_OUT,
  output [7:0] STORED_DATA
);

  wire [7:0] switch_8_bit_1_data_out;

  // Probe on STORED_DATA
  Register register_1 (.D(switch_8_bit_1_data_out), .en(SAVE), .clk(CLOCK), .Q(STORED_DATA));  // open: clr
  switch_8_bit switch_8_bit_1 (.DATA_IN(DATA_IN), .SWITCH(SAVE), .DATA_OUT(switch_8_bit_1_data_out));
  switch_8_bit switch_8_bit_2 (.DATA_IN(STORED_DATA), .SWITCH(LOAD), .DATA_OUT(DATA_OUT));
endmodule

module switch_1_bit (
  input  SWITCH,
  input  DATA_IN,
  output DATA_OUT
);

  wire not_1_out;

  not not_1 (not_1_out, SWITCH);
  Pull_Resistor pull_resistor_1 (.node(DATA_OUT));
  Transistor transistor_1 (.in(DATA_IN), .out(DATA_OUT), .gate(not_1_out));
endmodule

module switch_8_bit (
  input  SWITCH,
  input  [7:0] DATA_IN,
  output [7:0] DATA_OUT
);

  wire not_1_out;

  Pull_Resistor pull_resistor_1 (.node(DATA_OUT[7]));
  Pull_Resistor pull_resistor_2 (.node(DATA_OUT[3]));
  Pull_Resistor pull_resistor_3 (.node(DATA_OUT[6]));
  Pull_Resistor pull_resistor_4 (.node(DATA_OUT[2]));
  Pull_Resistor pull_resistor_5 (.node(DATA_OUT[5]));
  Pull_Resistor pull_resistor_6 (.node(DATA_OUT[1]));
  Pull_Resistor pull_resistor_7 (.node(DATA_OUT[4]));
  Pull_Resistor pull_resistor_8 (.node(DATA_OUT[0]));
  not not_1 (not_1_out, SWITCH);
  Transistor transistor_1 (.in(DATA_IN[0]), .out(DATA_OUT[0]), .gate(not_1_out));
  Transistor transistor_2 (.in(DATA_IN[1]), .out(DATA_OUT[1]), .gate(not_1_out));
  Transistor transistor_3 (.in(DATA_IN[2]), .out(DATA_OUT[2]), .gate(not_1_out));
  Transistor transistor_4 (.in(DATA_IN[3]), .out(DATA_OUT[3]), .gate(not_1_out));
  Transistor transistor_5 (.in(DATA_IN[4]), .out(DATA_OUT[4]), .gate(not_1_out));
  Transistor transistor_6 (.in(DATA_IN[5]), .out(DATA_OUT[5]), .gate(not_1_out));
  Transistor transistor_7 (.in(DATA_IN[6]), .out(DATA_OUT[6]), .gate(not_1_out));
  Transistor transistor_8 (.in(DATA_IN[7]), .out(DATA_OUT[7]), .gate(not_1_out));
endmodule

module not_8_bit (
  input  [7:0] in_1,
  output [7:0] out_2
);

  not not_1 (out_2[0], in_1[0]);
  not not_2 (out_2[1], in_1[1]);
  not not_3 (out_2[2], in_1[2]);
  not not_4 (out_2[3], in_1[3]);
  not not_5 (out_2[4], in_1[4]);
  not not_6 (out_2[5], in_1[5]);
  not not_7 (out_2[6], in_1[6]);
  not not_8 (out_2[7], in_1[7]);
endmodule

module and_8_bit (
  input  [7:0] ARG_1,
  input  [7:0] ARG_2,
  output [7:0] RESULT
);

  and and_1 (RESULT[0], ARG_1[0], ARG_2[0]);
  and and_2 (RESULT[1], ARG_1[1], ARG_2[1]);
  and and_3 (RESULT[2], ARG_1[2], ARG_2[2]);
  and and_4 (RESULT[3], ARG_1[3], ARG_2[3]);
  and and_5 (RESULT[4], ARG_1[4], ARG_2[4]);
  and and_6 (RESULT[5], ARG_1[5], ARG_2[5]);
  and and_7 (RESULT[6], ARG_1[6], ARG_2[6]);
  and and_8 (RESULT[7], ARG_1[7], ARG_2[7]);
endmodule

module or_8_bit (
  input  [7:0] ARG_1,
  input  [7:0] ARG_2,
  output [7:0] RESULT
);

  or or_1 (RESULT[0], ARG_1[0], ARG_2[0]);
  or or_2 (RESULT[1], ARG_1[1], ARG_2[1]);
  or or_3 (RESULT[2], ARG_1[2], ARG_2[2]);
  or or_4 (RESULT[3], ARG_1[3], ARG_2[3]);
  or or_5 (RESULT[4], ARG_1[4], ARG_2[4]);
  or or_6 (RESULT[5], ARG_1[5], ARG_2[5]);
  or or_7 (RESULT[6], ARG_1[6], ARG_2[6]);
  or or_8 (RESULT[7], ARG_1[7], ARG_2[7]);
endmodule

module xor_8_bit (
  input  [7:0] ARG_1,
  input  [7:0] ARG_2,
  output [7:0] RESULT
);

  xor xor_1 (RESULT[0], ARG_1[0], ARG_2[0]);
  xor xor_2 (RESULT[1], ARG_1[1], ARG_2[1]);
  xor xor_3 (RESULT[2], ARG_1[2], ARG_2[2]);
  xor xor_4 (RESULT[3], ARG_1[3], ARG_2[3]);
  xor xor_5 (RESULT[4], ARG_1[4], ARG_2[4]);
  xor xor_6 (RESULT[5], ARG_1[5], ARG_2[5]);
  xor xor_7 (RESULT[6], ARG_1[6], ARG_2[6]);
  xor xor_8 (RESULT[7], ARG_1[7], ARG_2[7]);
endmodule

module nand_8_bit (
  input  [7:0] ARG_1,
  input  [7:0] ARG_2,
  output [7:0] RESULT
);

  nand nand_1 (RESULT[0], ARG_1[0], ARG_2[0]);
  nand nand_2 (RESULT[1], ARG_1[1], ARG_2[1]);
  nand nand_3 (RESULT[2], ARG_1[2], ARG_2[2]);
  nand nand_4 (RESULT[3], ARG_1[3], ARG_2[3]);
  nand nand_5 (RESULT[4], ARG_1[4], ARG_2[4]);
  nand nand_6 (RESULT[5], ARG_1[5], ARG_2[5]);
  nand nand_7 (RESULT[6], ARG_1[6], ARG_2[6]);
  nand nand_8 (RESULT[7], ARG_1[7], ARG_2[7]);
endmodule

module nor_8_bit (
  input  [7:0] ARG_1,
  input  [7:0] ARG_2,
  output [7:0] RESULT
);

  nor nor_1 (RESULT[0], ARG_1[0], ARG_2[0]);
  nor nor_2 (RESULT[1], ARG_1[1], ARG_2[1]);
  nor nor_3 (RESULT[2], ARG_1[2], ARG_2[2]);
  nor nor_4 (RESULT[3], ARG_1[3], ARG_2[3]);
  nor nor_5 (RESULT[4], ARG_1[4], ARG_2[4]);
  nor nor_6 (RESULT[5], ARG_1[5], ARG_2[5]);
  nor nor_7 (RESULT[6], ARG_1[6], ARG_2[6]);
  nor nor_8 (RESULT[7], ARG_1[7], ARG_2[7]);
endmodule

module xnor_8_bit (
  input  [7:0] ARG_1,
  input  [7:0] ARG_2,
  output [7:0] RESULT
);

  wire xor_1_out, xor_2_out, xor_3_out, xor_4_out, xor_5_out, xor_6_out, xor_7_out, xor_8_out;

  xor xor_1 (xor_1_out, ARG_1[0], ARG_2[0]);
  not not_1 (RESULT[0], xor_1_out);
  xor xor_2 (xor_2_out, ARG_1[1], ARG_2[1]);
  not not_2 (RESULT[1], xor_2_out);
  xor xor_3 (xor_3_out, ARG_1[2], ARG_2[2]);
  not not_3 (RESULT[2], xor_3_out);
  xor xor_4 (xor_4_out, ARG_1[3], ARG_2[3]);
  not not_4 (RESULT[3], xor_4_out);
  xor xor_5 (xor_5_out, ARG_1[4], ARG_2[4]);
  not not_5 (RESULT[4], xor_5_out);
  xor xor_6 (xor_6_out, ARG_1[5], ARG_2[5]);
  not not_6 (RESULT[5], xor_6_out);
  xor xor_7 (xor_7_out, ARG_1[6], ARG_2[6]);
  not not_7 (RESULT[6], xor_7_out);
  xor xor_8 (xor_8_out, ARG_1[7], ARG_2[7]);
  not not_8 (RESULT[7], xor_8_out);
endmodule
