// Logisim project Arithmetic_8_Bit_Components.circ as structural Verilog: 9 circuits, main circuit adder_8_bit
module adder_8_bit (
  input  [7:0] ARG_1,
  input  CARRY_IN,
  input  [7:0] ARG_2,
  output [7:0] RESULT,
  output CARRY_OUT
);

  wire adder_1_bit_1_carry_out, adder_1_bit_2_carry_out, adder_1_bit_3_carry_out, adder_1_bit_4_carry_out,
       adder_1_bit_5_carry_out, adder_1_bit_6_carry_out, adder_1_bit_7_carry_out;

  // Probe on ARG_2
  // Probe on ARG_1
  adder_1_bit adder_1_bit_1 (
    .ARG_1(ARG_1[0]), .ARG_2(ARG_2[0]), .CARRY_IN(CARRY_IN), .SUM(RESULT[0]),
    .CARRY_OUT(adder_1_bit_1_carry_out));
  adder_1_bit adder_1_bit_2 (
    .ARG_1(ARG_1[1]), .ARG_2(ARG_2[1]), .CARRY_IN(adder_1_bit_1_carry_out), .SUM(RESULT[1]),
    .CARRY_OUT(adder_1_bit_2_carry_out));
  adder_1_bit adder_1_bit_3 (
    .ARG_1(ARG_1[2]), .ARG_2(ARG_2[2]), .CARRY_IN(adder_1_bit_2_carry_out), .SUM(RESULT[2]),
    .CARRY_OUT(adder_1_bit_3_carry_out));
  adder_1_bit adder_1_bit_4 (
    .ARG_1(ARG_1[3]), .ARG_2(ARG_2[3]), .CARRY_IN(adder_1_bit_3_carry_out), .SUM(RESULT[3]),
    .CARRY_OUT(adder_1_bit_4_carry_out));
  adder_1_bit adder_1_bit_5 (
    .ARG_1(ARG_1[4]), .ARG_2(ARG_2[4]), .CARRY_IN(adder_1_bit_4_carry_out), .SUM(RESULT[4]),
    .CARRY_OUT(adder_1_bit_5_carry_out));
  adder_1_bit adder_1_bit_6 (
    .ARG_1(ARG_1[5]), .ARG_2(ARG_2[5]), .CARRY_IN(adder_1_bit_5_carry_out), .SUM(RESULT[5]),
    .CARRY_OUT(adder_1_bit_6_carry_out));
  adder_1_bit adder_1_bit_7 (
    .ARG_1(ARG_1[6]), .ARG_2(ARG_2[6]), .CARRY_IN(adder_1_bit_6_carry_out), .SUM(RESULT[6]),
    .CARRY_OUT(adder_1_bit_7_carry_out));
  adder_1_bit adder_1_bit_8 (
    .ARG_1(ARG_1[7]), .ARG_2(ARG_2[7]), .CARRY_IN(adder_1_bit_7_carry_out), .SUM(RESULT[7]),
    .CARRY_OUT(CARRY_OUT));
  // Probe on RESULT
endmodule

module adder_1_bit (
  input  ARG_1,
  input  ARG_2,
  input  CARRY_IN,
  output SUM,
  output CARRY_OUT
);

  wire and_1_out, and_2_out, xor_1_out;

  and and_1 (and_1_out, ARG_1, ARG_2);
  xor xor_1 (xor_1_out, ARG_1, ARG_2);
  xor xor_2 (SUM, xor_1_out, CARRY_IN);
  and and_2 (and_2_out, xor_1_out, CARRY_IN);
  or or_1 (CARRY_OUT, and_2_out, and_1_out);
endmodule

module negator_8_bit (
  input  [7:0] ARG_IN,
  output [7:0] NEG_ARG
);

  wire [7:0] not_8_bit_1_out_2;

  // Probe on ARG_IN
  adder_8_bit adder_8_bit_1 (.ARG_2(not_8_bit_1_out_2), .ARG_1(8'h1), .RESULT(NEG_ARG));  // open: CARRY_IN, CARRY_OUT
  not_8_bit not_8_bit_1 (.in_1(ARG_IN), .out_2(not_8_bit_1_out_2));
  // Probe on NEG_ARG
endmodule

module equality (
  input  [7:0] ARG_1,
  input  [7:0] ARG_2,
  output EQUAL
);

  wire not_1_out, not_2_out, not_3_out, not_4_out, not_5_out, not_6_out, not_7_out, not_8_out,
       switch_1_bit_1_data_out, switch_1_bit_2_data_out, switch_1_bit_3_data_out, switch_1_bit_4_data_out,
       switch_1_bit_5_data_out, switch_1_bit_6_data_out, xor_1_out, xor_2_out, xor_3_out, xor_4_out,
       xor_5_out, xor_6_out, xor_7_out, xor_8_out;

  xor xor_1 (xor_1_out, ARG_1[0], ARG_2[0]);
  not not_1 (not_1_out, xor_1_out);
  xor xor_2 (xor_2_out, ARG_1[1], ARG_2[1]);
  not not_2 (not_2_out, xor_2_out);
  xor xor_3 (xor_3_out, ARG_1[2], ARG_2[2]);
  not not_3 (not_3_out, xor_3_out);
  xor xor_4 (xor_4_out, ARG_1[3], ARG_2[3]);
  not not_4 (not_4_out, xor_4_out);
  xor xor_5 (xor_5_out, ARG_1[4], ARG_2[4]);
  not not_5 (not_5_out, xor_5_out);
  xor xor_6 (xor_6_out, ARG_1[5], ARG_2[5]);
  not not_6 (not_6_out, xor_6_out);
  xor xor_7 (xor_7_out, ARG_1[6], ARG_2[6]);
  not not_7 (not_7_out, xor_7_out);
  xor xor_8 (xor_8_out, ARG_1[7], ARG_2[7]);
  not not_8 (not_8_out, xor_8_out);
  switch_1_bit switch_1_bit_1 (.SWITCH(not_1_out), .DATA_IN(not_2_out), .DATA_OUT(switch_1_bit_1_data_out));
  switch_1_bit switch_1_bit_2 (.SWITCH(not_3_out), .DATA_IN(not_4_out), .DATA_OUT(switch_1_bit_2_data_out));
  switch_1_bit switch_1_bit_3 (.SWITCH(not_5_out), .DATA_IN(not_6_out), .DATA_OUT(switch_1_bit_3_data_out));
  switch_1_bit switch_1_bit_4 (.SWITCH(not_7_out), .DATA_IN(not_8_out), .DATA_OUT(switch_1_bit_4_data_out));
  switch_1_bit switch_1_bit_5 (
    .SWITCH(switch_1_bit_1_data_out), .DATA_IN(switch_1_bit_2_data_out), .DATA_OUT(switch_1_bit_5_data_out));
  switch_1_bit switch_1_bit_6 (
    .SWITCH(switch_1_bit_3_data_out), .DATA_IN(switch_1_bit_4_data_out), .DATA_OUT(switch_1_bit_6_data_out));
  switch_1_bit switch_1_bit_7 (.SWITCH(switch_1_bit_5_data_out), .DATA_IN(switch_1_bit_6_data_out), .DATA_OUT(EQUAL));
endmodule

module multiplier_8_bit (
  input  [7:0] ARGUMENT_1,
  input  [7:0] ARGUMENT_2,
  output [15:0] PRODUCT_16_BIT,
  output [7:0] LOWER_BYTE,
  output [7:0] UPPER_BYTE
);

  // Probe on ARGUMENT_1
  // Probe on ARGUMENT_2
  Multiplier multiplier_1 (.a(ARGUMENT_1), .b(ARGUMENT_2), .out(LOWER_BYTE), .cout(PRODUCT_16_BIT[15:8]));  // open: cin
  // Probe on {PRODUCT_16_BIT[15:8], LOWER_BYTE}
  // Probe on LOWER_BYTE
  // Probe on PRODUCT_16_BIT[15:8]

  assign PRODUCT_16_BIT[7:0] = LOWER_BYTE;
  assign UPPER_BYTE = PRODUCT_16_BIT[15:8];
endmodule

module divider_8_bit (
  input  [7:0] ARGUMENT_1,
  input  [7:0] ARGUMENT_2,
  output [7:0] QUOTIENT,
  output [7:0] REMAINDER
);

  // Probe on ARGUMENT_1
  // Probe on ARGUMENT_2
  Divider divider_1 (.a(ARGUMENT_1), .b(ARGUMENT_2), .out(QUOTIENT), .rem(REMAINDER));  // open: upper
  // Probe on QUOTIENT
  // Probe on REMAINDER
endmodule

module less_unsigned (
  input  [7:0] ARG_1,
  input  [7:0] ARG_2,
  output LESS
);

  wire adder_8_bit_1_carry_out, equality_1_equal, not_1_out, not_2_out;
  wire [7:0] not_8_bit_1_out_2;

  // Probe on ARG_1
  // Probe on ARG_2
  equality equality_1 (.ARG_2(ARG_2), .ARG_1(ARG_1), .EQUAL(equality_1_equal));
  not_8_bit not_8_bit_1 (.in_1(ARG_2), .out_2(not_8_bit_1_out_2));
  not not_1 (not_1_out, equality_1_equal);
  adder_8_bit adder_8_bit_1 (
    .ARG_2(not_8_bit_1_out_2), .ARG_1(ARG_1), .CARRY_OUT(adder_8_bit_1_carry_out));  // open: CARRY_IN, RESULT
  not not_2 (not_2_out, adder_8_bit_1_carry_out);
  LED led_1 (.in(LESS));
  and and_1 (LESS, not_1_out, not_2_out);

  // Notes on the sheet:
  //   Is ARG_1 Less than ARG_2?
  //   (Unsigned Comparison)
endmodule

module less_signed (
  input  [7:0] ARG_1,
  input  [7:0] ARG_2,
  output LESS
);

  wire [7:0] not_8_bit_1_out_2, xor_8_bit_1_result, xor_8_bit_2_result;

  // Probe on ARG_1
  // Probe on ARG_2
  xor_8_bit xor_8_bit_1 (.ARG_2(ARG_1), .ARG_1(8'h80), .RESULT(xor_8_bit_1_result));
  xor_8_bit xor_8_bit_2 (.ARG_2(8'h80), .ARG_1(ARG_2), .RESULT(xor_8_bit_2_result));
  not_8_bit not_8_bit_1 (.in_1(xor_8_bit_1_result), .out_2(not_8_bit_1_out_2));
  adder_8_bit adder_8_bit_1 (
    .ARG_2(xor_8_bit_2_result), .ARG_1(not_8_bit_1_out_2), .CARRY_OUT(LESS));  // open: CARRY_IN, RESULT

  // Notes on the sheet:
  //   Is ARG_1 Less than ARG_2?
  //   (Signed Comparison)
endmodule

module mult_by_4 (
  input  [7:0] ARGUMENT_1,
  output [15:0] PRODUCT_16_BIT
);

  // Probe on ARGUMENT_1
  // Probe on 8'h4
  Multiplier multiplier_1 (
    .a(ARGUMENT_1), .b(8'h4), .out(PRODUCT_16_BIT[7:0]), .cout(PRODUCT_16_BIT[15:8]));  // open: cin
  // Probe on PRODUCT_16_BIT
endmodule
